// Logisim project LogisimCircuits.circ as structural Verilog: 1 circuit, main circuit main
module main (
  input  in_1,
  input  in_2,
  input  in_3,
  input  in_4,
  input  in_5,
  input  in_6,
  input  in_7,
  input  in_8,
  input  in_9,
  input  in_10,
  input  in_11,
  input  in_12,
  input  in_13,
  input  in_14,
  input  in_15,
  input  in_16,
  input  in_17,
  input  in_18,
  input  in_19,
  input  in_20,
  input  in_21,
  input  in_22,
  input  in_23,
  input  in_24,
  input  in_25,
  input  in_26,
  input  in_27,
  input  in_28,
  input  in_29,
  input  in_30,
  input  in_31,
  input  in_32,
  input  in_33,
  input  in_34,
  input  in_35,
  input  in_36,
  input  in_37,
  input  in_38,
  input  in_39,
  input  in_40,
  input  in_41,
  input  in_42,
  input  in_43,
  input  in_44,
  input  in_45,
  input  in_46,
  input  in_47,
  input  in_48,
  input  in_49,
  input  in_50,
  input  A,
  input  A_2,
  input  B,
  input  B_2,
  input  A_3,
  input  A_4,
  input  B_3,
  input  B_4,
  output out_59,
  output out_60,
  output out_61,
  output out_62,
  output out_63,
  output out_64,
  output out_65,
  output out_66,
  output NOT,
  output out_68,
  output NAND,
  output out_70,
  output out_71,
  output out_72,
  output out_73,
  output out_74,
  output out_75,
  output out_76,
  output out_77,
  output out_78,
  output NOR,
  output out_80,
  output out_81,
  output out_82,
  output out_83,
  output out_84,
  output out_85,
  output out_86,
  output out_87,
  output out_88
);

  wire and_3_out, and_4_out, and_5_out, and_6_out, and_9_out, and_10_out, and_11_out, and_12_out, not_2_out,
       not_3_out, not_4_out, not_5_out, not_7_out, not_8_out, not_9_out, not_10_out;

  and and_1 (out_59, in_1, in_5);
  and and_2 (out_65, in_11, in_15);
  not not_1 (NOT, in_17);
  nand nand_1 (NAND, in_19, in_23);
  nand nand_2 (out_75, in_29, in_33);
  xor xor_1 (out_77, in_35, in_39);
  xor xor_2 (out_83, in_45, in_49);
  not not_2 (not_2_out, A);
  not not_3 (not_3_out, B);
  not not_4 (not_4_out, A_4);
  not not_5 (not_5_out, B_4);
  and and_3 (and_3_out, not_2_out, B);
  and and_4 (and_4_out, A, not_3_out);
  and and_5 (and_5_out, not_4_out, B_4);
  and and_6 (and_6_out, A_4, not_5_out);
  and and_7 (out_60, in_2, in_6);
  and and_8 (out_63, in_9, in_13);
  not not_6 (out_68, in_18);
  nand nand_3 (out_70, in_20, in_24);
  nand nand_4 (out_73, in_27, in_31);
  xor xor_3 (out_78, in_36, in_40);
  xor xor_4 (out_81, in_43, in_47);
  or or_1 (out_85, and_3_out, and_4_out);
  or or_2 (out_88, and_5_out, and_6_out);
  or or_3 (out_61, in_3, in_7);
  or or_4 (out_66, in_12, in_16);
  not not_7 (not_7_out, A_2);
  not not_8 (not_8_out, B_2);
  not not_9 (not_9_out, A_3);
  not not_10 (not_10_out, B_3);
  xor xor_5 (out_71, in_21, in_25);
  xor xor_6 (out_76, in_30, in_34);
  nor nor_1 (NOR, in_37, in_41);
  nor nor_2 (out_84, in_46, in_50);
  and and_9 (and_9_out, not_7_out, B_2);
  and and_10 (and_10_out, A_2, not_8_out);
  and and_11 (and_11_out, not_9_out, B_3);
  and and_12 (and_12_out, A_3, not_10_out);
  or or_5 (out_62, in_4, in_8);
  or or_6 (out_64, in_10, in_14);
  or or_7 (out_86, and_9_out, and_10_out);
  or or_8 (out_87, and_11_out, and_12_out);
  xor xor_7 (out_72, in_22, in_26);
  xor xor_8 (out_74, in_28, in_32);
  nor nor_3 (out_80, in_38, in_42);
  nor nor_4 (out_82, in_44, in_48);

  // Notes on the sheet:
  //   XOR
  //   AND
  //   OR
  //   XNOR
endmodule
