// Logisim project Logisim Circuits.circ as structural Verilog: 1 circuit, main circuit main
module main (
  input  A,
  input  B,
  input  A_2,
  input  B_2,
  input  Cin,
  input  A_3,
  input  B_3,
  input  C,
  input  a0,
  input  a1,
  input  a2,
  input  a3,
  input  a4,
  input  a5,
  input  a6,
  input  a7,
  input  S2,
  input  S1,
  input  S0,
  output out_20,
  output out_21,
  output Sum,
  output Count,
  output _0,
  output _1,
  output _2,
  output _3,
  output _4,
  output _5,
  output _6,
  output _7,
  output out_32
);

  wire and_2_out, and_11_out, and_12_out, and_13_out, and_14_out, and_15_out, and_16_out, and_17_out,
       and_18_out, and_19_out, not_1_out, not_2_out, not_3_out, not_4_out, not_5_out, not_6_out, xor_2_out;

  xor xor_1 (out_20, A, B);
  and and_1 (out_21, A, B);
  not not_1 (not_1_out, A_3);
  not not_2 (not_2_out, B_3);
  not not_3 (not_3_out, C);
  xor xor_2 (xor_2_out, A_2, B_2);
  and and_2 (and_2_out, A_2, B_2);
  and and_3 (_0, not_1_out, not_2_out, not_3_out);
  and and_4 (_1, not_1_out, not_2_out, C);
  and and_5 (_2, not_1_out, B_3, not_3_out);
  and and_6 (_3, not_1_out, B_3, C);
  and and_7 (_4, not_3_out, not_2_out, A_3);
  and and_8 (_5, A_3, not_2_out, C);
  and and_9 (_6, A_3, B_3, not_3_out);
  and and_10 (_7, A_3, B_3, C);
  not not_4 (not_4_out, S2);
  not not_5 (not_5_out, S1);
  and and_11 (and_11_out, xor_2_out, Cin);
  not not_6 (not_6_out, S0);
  xor xor_3 (Sum, xor_2_out, Cin);
  or or_1 (Count, and_11_out, and_2_out);
  and and_12 (and_12_out, a5, not_5_out, S0);
  and and_13 (and_13_out, a0, not_4_out, not_5_out, not_6_out);
  and and_14 (and_14_out, a1, not_4_out, not_5_out, S0);
  and and_15 (and_15_out, a2, not_4_out, S1, not_6_out);
  and and_16 (and_16_out, a3, not_4_out, S1, S0);
  and and_17 (and_17_out, a4, S2, not_5_out, not_6_out);
  and and_18 (and_18_out, a6, S2, S1, not_6_out);
  and and_19 (and_19_out, a7, S2, S1, S0);
  or or_2 (out_32, and_13_out, and_14_out, and_15_out, and_16_out, and_17_out, and_12_out, and_18_out, and_19_out);

  // Notes on the sheet:
  //   Half Adder
  //   3x8 Decoder
  //   Full Adder
  //   sum1
  //   C1
endmodule
