// Logisim project lab3AllTasksCircuit.circ as structural Verilog: 1 circuit, main circuit main
module main (
  input  A0,
  input  A1,
  input  A2,
  input  A3,
  input  B0,
  input  B1,
  input  B2,
  input  B3,
  input  _0,
  output O3,
  output O2,
  output O1,
  output O0,
  output out_14,
  output Signed_Over_Flow
);

  wire and_1_out, and_2_out, and_4_out, and_6_out, and_7_out, and_8_out, and_9_out, and_10_out, or_1_out,
       or_2_out, or_3_out, xor_1_out, xor_2_out, xor_4_out, xor_5_out, xor_8_out, xor_9_out, xor_11_out,
       xor_12_out;

  xor xor_1 (xor_1_out, _0, B0);
  xor xor_2 (xor_2_out, xor_1_out, A0);
  and and_1 (and_1_out, xor_1_out, A0);
  and and_2 (and_2_out, xor_2_out, _0);
  xor xor_3 (O0, xor_2_out, _0);
  or or_1 (or_1_out, and_2_out, and_1_out);
  xor xor_4 (xor_4_out, B1, _0);
  // AND_Gate and_3 is placed but not wired
  xor xor_5 (xor_5_out, xor_4_out, A1);
  and and_4 (and_4_out, xor_4_out, A1);
  // XOR_Gate xor_6 is placed but not wired
  // AND_Gate and_5 is placed but not wired
  and and_6 (and_6_out, xor_5_out, or_1_out);
  xor xor_7 (O1, xor_5_out, or_1_out);
  or or_2 (or_2_out, and_6_out, and_4_out);
  xor xor_8 (xor_8_out, B2, _0);
  xor xor_9 (xor_9_out, xor_8_out, A2);
  and and_7 (and_7_out, xor_8_out, A2);
  xor xor_10 (O2, xor_9_out, or_2_out);
  and and_8 (and_8_out, xor_9_out, or_2_out);
  or or_3 (or_3_out, and_8_out, and_7_out);
  xor xor_11 (xor_11_out, B3, _0);
  xor xor_12 (xor_12_out, xor_11_out, A3);
  and and_9 (and_9_out, xor_11_out, A3);
  xor xor_13 (O3, xor_12_out, or_3_out);
  and and_10 (and_10_out, xor_12_out, or_3_out);
  or or_4 (out_14, and_10_out, and_9_out);
  xor xor_14 (Signed_Over_Flow, out_14, or_3_out);

  // Notes on the sheet:
  //   Control Input
  //   1-->-
  //   Cin
  //   Unsigned overflow
  //   C1
  //   Full Adder
  //   sum1
  //   C1
  //   sum1
  //   Full Adder
  //   C1
  //   sum1
  //   Full Adder
  //   C1
  //   sum1
  //   Full Adder
endmodule
